# Fritzing sketch wiring (saved by Fritzing 0.9.10b)
circuit board: 11.5846cm x 6.52361cm
breadboards: 3

parts:
  MH-ET_LIVE_ESP32_DEVKIT1 = MH-ET LIVE ESP32 DEVKIT 38 pins
  LCD1 = 1_7in tft lcd
  RE1 = Rotary Encoder [package=THT]
  Switch_2 = Pushbutton [package="[THT]"]
  Switch_1 = Pushbutton [package="[THT]"]
  R1 = Resistor [tolerance=±5% resistance=10k package="2512 [SMD]"]
  R2 = Resistor [tolerance=±5% resistance=10k package="2512 [SMD]"]
  R3 = Resistor [tolerance=±5% resistance=10k package="2512 [SMD]"]
  R4 = Resistor [tolerance=±5% resistance=10k package="2512 [SMD]"]
  C1 = Ceramic Capacitor [capacitance="100 nF" voltage=35V package="0603 [SMD, multilayer]"]
  C2 = Ceramic Capacitor [capacitance="100 nF" voltage=35V package="0603 [SMD, multilayer]"]
  Mod1 = Passive Buzzer

nets:
  N1: MH-ET_LIVE_ESP32_DEVKIT1.3V3, LCD1.pin_8, LCD1.pin_9
  N2: MH-ET_LIVE_ESP32_DEVKIT1.GND#58, LCD1.pin_1, LCD1.pin_14, RE1.EncoderPinC, Switch_2.Pin_3, Switch_2.Pin_4, Switch_1.Pin_1, Switch_1.Pin_2, C1.0, C2.1, Mod1.-
  N3: MH-ET_LIVE_ESP32_DEVKIT1.5V, LCD1.pin2, R1.Pin_1, R2.Pin_1
  N4: MH-ET_LIVE_ESP32_DEVKIT1.IO23, LCD1.pin4
  N5: MH-ET_LIVE_ESP32_DEVKIT1.IO21, Switch_2.Pin_1, Switch_2.Pin_2
  N6: MH-ET_LIVE_ESP32_DEVKIT1.IO18, LCD1.pin3
  N7: MH-ET_LIVE_ESP32_DEVKIT1.IO5, Switch_1.Pin_3, Switch_1.Pin_4
  N8: MH-ET_LIVE_ESP32_DEVKIT1.IO17, R3.Pin_0, C2.0
  N9: MH-ET_LIVE_ESP32_DEVKIT1.IO16, R4.Pin_0, C1.1
  N10: MH-ET_LIVE_ESP32_DEVKIT1.IO4, LCD1.pin_5
  N11: MH-ET_LIVE_ESP32_DEVKIT1.IO2, LCD1.pin_6
  N12: MH-ET_LIVE_ESP32_DEVKIT1.IO15, LCD1.pin_7
  N13: RE1.EncoderPinA, R2.Pin_0, R3.Pin_1
  N14: RE1.EncoderPinB, R1.Pin_0, R4.Pin_1

custom parts:
  MH-ET LIVE ESP32 DEVKIT 38 pins: http://mh.nodebb.com/topic/2/mh-et-live-esp32-devkit
  1_7in tft lcd: This is the Zoll 1.77in spi lcd display. The 1.77" display has 128x160 color pixels.
